# Fritzing sketch Wiring (saved by Fritzing 1.0.5)
breadboards: 3

parts:
  U1 = ESP32S-HiLetgo [part_number=ESP32S-HiLetgo]
  Part1 = Motor Driver 1A Dual TB6612FNG  # not connected
  Part2 = Motor Driver 1A Dual TB6612FNG  # not connected
  Part3 = Motor Driver 1A Dual TB6612FNG  # not connected
  C1 = Tantalum Capacitor [capacitance=1μF voltage=35V package="200 mil [THT, tantalum]"]
  C2 = Tantalum Capacitor [capacitance=1μF voltage=35V package="200 mil [THT, tantalum]"]
  C3 = Tantalum Capacitor [capacitance=1μF voltage=35V package="200 mil [THT, tantalum]"]
  M2 = DC Motor [voltage_(max)=6V voltage_(min)=3V]  # not connected
  M3 = DC Motor [voltage_(max)=6V voltage_(min)=3V]  # not connected
  M4 = DC Motor [voltage_(max)=6V voltage_(min)=3V]  # not connected
  M5 = DC Motor [voltage_(max)=6V voltage_(min)=3V]  # not connected
  M6 = DC Motor [voltage_(max)=6V voltage_(min)=3V]  # not connected
  M7 = DC Motor [voltage_(max)=6V voltage_(min)=3V]  # not connected
  U2 = Voltage Regulator - 5V [package="TO220 [THT]"]
  VCC1 = 4 x AAA Battery Mount [internal_resistance=0.1Ω]
  J5 = Basic Servo
  J6 = Basic Servo
  J7 = Basic Servo
  J8 = Basic Servo

nets:
  N1: U1.3.3, C1.+, C2.+, C3.+
  N2: U1.GND, VCC1.-
  N3: U1.GPIO17, J5.pulse
  N4: U1.GPIO5, J6.pulse
  N5: U1.GPIO18, J8.pulse
  N6: U1.GPIO19, J7.pulse
  N7: U2.input_voltage, VCC1.+
  GND: U2.GND, J5.gnd, J6.gnd, J7.gnd, J8.gnd
  VCC: U2.output_voltage, J5.vcc, J6.vcc, J7.vcc, J8.vcc

custom parts:
  ESP32S-HiLetgo: HiLetgo ESP-WROOM-32 ESP32 ESP-32S Development Board 2.4GHz Dual-Mode WiFi + Bluetooth Dual Cores Microcontroller The ESP32 integrated with Antenna switches, RF Balun, power amplifiers, low-noise amplifiers, filters, and management modules, and the entire solution occupies the least area of PCB. 2.4 GHz Wi-Fi plus Bluetooth dual-mode chip, with TSMC Ultra-low power consumption 40nm technology,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
